// Logisim project diagrama do processador.circ as structural Verilog: 6 circuits, main circuit main
module main (
  input  [1:0] XY,
  input  [3:0] B,
  input  [3:0] A,
  output out_4,
  output out_5,
  output [3:0] S,
  output [3:0] S_2,
  output [3:0] S_3
);

  Add_4 add_4_1 (.A(A), .B(B), .overflow(out_4), .S(S_2));
  Sub_4 sub_4_1 (.A(A), .B(B), .out_4(S_3), .out_3(out_5));
  Rot_esq rot_esq_1 (.ABCD(A), .XY(XY), .ABCD_2(S));
endmodule

module Add_1 (
  input  A,
  input  B,
  input  C,
  output S,
  output Vai_1
);

  wire and_1_out, and_2_out, or_1_out, xor_1_out;

  xor xor_1 (xor_1_out, C, B);
  xor xor_2 (S, xor_1_out, A);
  or or_1 (or_1_out, C, B);
  and and_1 (and_1_out, or_1_out, A);
  and and_2 (and_2_out, C, B);
  or or_2 (Vai_1, and_1_out, and_2_out);
endmodule

module Sub_1 (
  input  A,
  input  B,
  input  C,
  output S,
  output Vai_1
);

  wire and_1_out, and_2_out, or_1_out, xor_1_out;

  or or_1 (or_1_out, C, B);
  xor xor_1 (xor_1_out, C, B);
  xor xor_2 (S, xor_1_out, A);
  and and_1 (and_1_out, or_1_out, ~A);  // AND_Gate
  and and_2 (and_2_out, C, B);
  or or_2 (Vai_1, and_1_out, and_2_out);
endmodule

module Add_4 (
  input  [3:0] B,
  input  [3:0] A,
  output overflow,
  output [3:0] S
);

  wire add_1_1_p5, add_1_2_p4, add_1_2_p8;

  // Add_1 add_1_1: pin names not known; wires that end beside it: overflow, A[3], S[3], B[3], add_1_1_p5, A[2]
  // Add_1 add_1_2: pin names not known; wires that end beside it: A[2], S[2], B[2], add_1_2_p4, A[1], S[1], B[1], add_1_2_p8, A[0]
  // Add_1 add_1_3: pin names not known; wires that end beside it: A[3], S[3], B[3], add_1_1_p5, A[2], S[2], B[2], add_1_2_p4, A[1]
  // Add_1 add_1_4: pin names not known; wires that end beside it: A[1], S[1], B[1], add_1_2_p8, A[0], S[0], B[0], 1'b0
endmodule

module Sub_4 (
  input  [3:0] B,
  input  [3:0] A,
  output out_3,
  output [3:0] out_4
);

  wire sub_1_2_vai_1, sub_1_3_vai_1, sub_1_4_vai_1;

  Sub_1 sub_1_1 (.S(out_4[3]), .Vai_1(out_3), .A(A[3]), .B(B[3]), .C(sub_1_2_vai_1));
  Sub_1 sub_1_2 (.S(out_4[2]), .Vai_1(sub_1_2_vai_1), .A(A[2]), .B(B[2]), .C(sub_1_3_vai_1));
  Sub_1 sub_1_3 (.S(out_4[1]), .Vai_1(sub_1_3_vai_1), .A(A[1]), .B(B[1]), .C(sub_1_4_vai_1));
  Sub_1 sub_1_4 (.S(out_4[0]), .Vai_1(sub_1_4_vai_1), .A(A[0]), .B(B[0]), .C(1'b0));
endmodule

module Rot_esq (
  input  [3:0] ABCD,
  input  [1:0] XY,
  output [3:0] ABCD_2
);

  wire and_1_out, and_2_out, and_3_out, and_4_out, and_5_out, and_6_out, and_7_out, and_8_out, and_9_out;

  and and_1 (and_1_out, ~XY[1], ~XY[0], ABCD[3]);  // AND_Gate
  and and_2 (and_2_out, ~XY[1], XY[0], ABCD[2]);  // AND_Gate
  and and_3 (and_3_out, XY[1], ~XY[0], ABCD[1]);  // AND_Gate
  and and_4 (and_4_out, XY[1], XY[0], ABCD[0]);
  and and_5 (and_5_out, ~XY[1], ~XY[0], ABCD[2]);  // AND_Gate
  and and_6 (and_6_out, ~XY[1], XY[0], ABCD[1]);  // AND_Gate
  and and_7 (and_7_out, XY[1], ~XY[0], ABCD[0]);  // AND_Gate
  and and_8 (and_8_out, ~XY[1], ~XY[0], ABCD[1]);  // AND_Gate
  and and_9 (and_9_out, ~XY[1], XY[0], ABCD[0]);  // AND_Gate
  and and_10 (ABCD_2[0], ~XY[1], ~XY[0], ABCD[0]);  // AND_Gate
  or or_1 (ABCD_2[3], and_1_out, and_2_out, and_3_out, and_4_out);
  or or_2 (ABCD_2[2], and_5_out, and_6_out, and_7_out);
  or or_3 (ABCD_2[1], and_8_out, and_9_out);
endmodule
